// Logisim project vj1.circ as structural Verilog: 18 circuits, main circuit main
module main (
  input  a,
  input  b,
  input  s,
  output o
);

  wire and_1_out, and_2_out;

  and and_1 (and_1_out, a, s);
  and and_2 (and_2_out, b, ~s);  // AND_Gate
  or or_1 (o, and_1_out, and_2_out);
endmodule

module mux2to1 (
  input  a,
  input  b,
  input  s,
  output o
);

  wire and_1_out, and_2_out, not_1_out;

  not not_1 (not_1_out, s);
  and and_1 (and_1_out, a, s);
  and and_2 (and_2_out, b, not_1_out);
  or or_1 (o, and_1_out, and_2_out);
endmodule

module mux4to1 (
  input  a,
  input  b,
  input  c,
  input  d,
  input  [1:0] in_5,
  output o
);

  wire mux2to1_1_o, mux2to1_2_o;

  mux2to1 mux2to1_1 (.o(mux2to1_1_o), .s(in_5[0]), .b(b), .a(a));
  mux2to1 mux2to1_2 (.o(mux2to1_2_o), .s(in_5[0]), .b(d), .a(c));
  mux2to1 mux2to1_3 (.o(o), .s(in_5[1]), .b(mux2to1_2_o), .a(mux2to1_1_o));
endmodule

module SRLatch (
  input  r,
  input  s,
  output q,
  output qn
);

  nor nor_1 (q, r, qn);
  nor nor_2 (qn, q, s);
endmodule

module DLatch (
  input  c,
  input  d,
  output q
);

  wire and_1_out, and_2_out;

  and and_1 (and_1_out, c, ~d);  // AND_Gate
  and and_2 (and_2_out, c, d);
  SRLatch srlatch_1 (.r(and_1_out), .s(and_2_out), .q(q));  // open: qn
endmodule

module DFlipFlop (
  input  c,
  input  d,
  output q
);

  wire dlatch_1_q, not_1_out;

  not not_1 (not_1_out, c);
  DLatch dlatch_1 (.c(c), .d(d), .q(dlatch_1_q));
  DLatch dlatch_2 (.c(not_1_out), .d(dlatch_1_q), .q(q));
endmodule

module Reg4b (
  input  c,
  input  WriteEn,
  input  [3:0] data,
  output [3:0] out_4
);

  wire and_1_out;

  and and_1 (and_1_out, c, WriteEn);
  DFlipFlop dflipflop_1 (.c(and_1_out), .d(data[3]), .q(out_4[3]));
  DFlipFlop dflipflop_2 (.c(and_1_out), .d(data[2]), .q(out_4[2]));
  DFlipFlop dflipflop_3 (.c(and_1_out), .d(data[1]), .q(out_4[1]));
  DFlipFlop dflipflop_4 (.c(and_1_out), .d(data[0]), .q(out_4[0]));
endmodule

module RegFile (
  input  [3:0] in_1,
  input  [1:0] RA,
  input  C,
  input  WriteEn,
  input  [3:0] in_5,
  input  [3:0] in_6,
  input  [1:0] RB,
  input  [1:0] RW,
  input  [3:0] BusW
);

  wire and_1_out, and_2_out, and_3_out, decoder_1_out0, decoder_1_out1, decoder_1_out2, decoder_1_out3,
       decoder_2_out0, decoder_2_out1, decoder_2_out2, decoder_2_out3;
  wire [3:0] controlled_buffer_1_out, Reg1_out_4, Reg2_out_4, Reg3_out_4;

  Decoder #(.select(2)) decoder_1 (
    .out0(decoder_1_out0), .out1(decoder_1_out1), .out2(decoder_1_out2), .out3(decoder_1_out3), .sel(RA),
    .en(1'b1));
  Decoder #(.select(2)) decoder_2 (
    .out0(decoder_2_out0), .out1(decoder_2_out1), .out2(decoder_2_out2), .out3(decoder_2_out3), .sel(RW),
    .en(1'b1));
  and and_1 (and_1_out, decoder_2_out1, WriteEn);
  Reg4b Reg0 (.c(C), .data(BusW));  // open: WriteEn, out_4
  Reg4b Reg2 (.c(C), .WriteEn(and_1_out), .data(BusW), .out_4(Reg2_out_4));
  assign controlled_buffer_1_out = decoder_1_out3 ? Reg2_out_4 : 4'bz;  // Controlled_Buffer controlled_buffer_1
  Controlled_Buffer #(.width(4)) controlled_buffer_2 (.in(Reg2_out_4), .out(controlled_buffer_1_out));  // open: en
  and and_2 (and_2_out, decoder_2_out2, WriteEn);
  and and_3 (and_3_out, decoder_2_out3, WriteEn);
  Reg4b Reg1 (.c(C), .WriteEn(and_2_out), .data(BusW), .out_4(Reg1_out_4));
  Reg4b Reg3 (.c(C), .WriteEn(and_3_out), .data(BusW), .out_4(Reg3_out_4));
  assign controlled_buffer_1_out = decoder_1_out0 ? in_1 : 4'bz;  // Controlled_Buffer controlled_buffer_3
  assign controlled_buffer_1_out = decoder_1_out1 ? Reg1_out_4 : 4'bz;  // Controlled_Buffer controlled_buffer_4
  assign controlled_buffer_1_out = decoder_1_out2 ? Reg3_out_4 : 4'bz;  // Controlled_Buffer controlled_buffer_5
  Controlled_Buffer #(.width(4)) controlled_buffer_6 (.in(Reg3_out_4), .out(controlled_buffer_1_out));  // open: en
  Controlled_Buffer #(.width(4)) controlled_buffer_7 (.in(Reg1_out_4), .out(controlled_buffer_1_out));  // open: en
  // also tied to GND on the sheet: decoder_2_out0
endmodule

module adder1b (
  input  a,
  input  b,
  input  cin,
  output s,
  output cout
);

  wire and_1_out, and_2_out, and_3_out, and_4_out, and_5_out, and_6_out, and_7_out, not_1_out, not_2_out,
       not_3_out, not_4_out, not_5_out, not_6_out;

  not not_1 (not_1_out, a);
  not not_2 (not_2_out, b);
  not not_3 (not_3_out, a);
  not not_4 (not_4_out, cin);
  not not_5 (not_5_out, b);
  not not_6 (not_6_out, cin);
  and and_1 (and_1_out, b, cin);
  and and_2 (and_2_out, a, cin);
  and and_3 (and_3_out, a, b);
  and and_4 (and_4_out, not_1_out, not_2_out, cin);
  and and_5 (and_5_out, not_3_out, b, not_4_out);
  and and_6 (and_6_out, a, not_5_out, not_6_out);
  and and_7 (and_7_out, a, b, cin);
  or or_1 (cout, and_1_out, and_2_out, and_3_out);
  or or_2 (s, and_4_out, and_5_out, and_6_out, and_7_out);
endmodule

module adder8b (
  input  [7:0] A,
  input  Cin,
  input  [7:0] B,
  output Overflow,
  output [7:0] S
);

  wire adder1b_1_cout, adder1b_2_cout, adder1b_3_cout, adder1b_4_cout, adder1b_5_cout, adder1b_6_cout,
       adder1b_7_cout;

  adder1b adder1b_1 (.cout(adder1b_1_cout), .s(S[0]), .b(B[0]), .a(A[0]), .cin(Cin));
  adder1b adder1b_2 (.cout(adder1b_2_cout), .s(S[1]), .b(B[1]), .a(A[1]), .cin(adder1b_1_cout));
  adder1b adder1b_3 (.cout(adder1b_3_cout), .s(S[2]), .b(B[2]), .a(A[2]), .cin(adder1b_2_cout));
  adder1b adder1b_4 (.cout(adder1b_4_cout), .s(S[3]), .b(B[3]), .a(A[3]), .cin(adder1b_3_cout));
  adder1b adder1b_5 (.cout(adder1b_5_cout), .s(S[4]), .b(B[4]), .a(A[4]), .cin(adder1b_4_cout));
  adder1b adder1b_6 (.cout(adder1b_6_cout), .s(S[5]), .b(B[5]), .a(A[5]), .cin(adder1b_5_cout));
  adder1b adder1b_7 (.cout(adder1b_7_cout), .s(S[6]), .b(B[6]), .a(A[6]), .cin(adder1b_6_cout));
  adder1b adder1b_8 (.cout(Overflow), .s(S[7]), .b(B[7]), .a(A[7]), .cin(adder1b_7_cout));
endmodule

module alu8 (
  input  [7:0] A,
  input  [7:0] B,
  input  [3:0] Op,
  output out_4,
  output [7:0] out_5
);

  wire aluctrl_1_t, aluctrl_1_y;
  wire [1:0] aluctrl_1_x0;
  wire [7:0] adder8b_1_s, and_1_out, bit_extender_1_out, multiplexer_1_out, nor_1_out, or_1_out, xor_1_out,
       xor_2_out;

  // Probe on A
  // Probe on B
  aluctrl aluctrl_1 (.in_1(Op), .T(aluctrl_1_t), .X1(aluctrl_1_x0[1]), .X0(aluctrl_1_x0[0]), .Y(aluctrl_1_y));
  assign bit_extender_1_out = {{7{aluctrl_1_t}}, aluctrl_1_t};  // Bit_Extender bit_extender_1
  assign xor_1_out = B ^ bit_extender_1_out;  // XOR_Gate xor_1, 8 bits wide
  assign and_1_out = A & B;  // AND_Gate and_1, 8 bits wide
  assign or_1_out = A | B;  // OR_Gate or_1, 8 bits wide
  assign xor_2_out = A ^ B;  // XOR_Gate xor_2, 8 bits wide
  assign nor_1_out = ~(A | B);  // NOR_Gate nor_1, 8 bits wide
  Multiplexer #(.select(2), .width(8), .enable("false")) multiplexer_1 (
    .in0(and_1_out), .in1(or_1_out), .in2(xor_2_out), .in3(nor_1_out), .out(multiplexer_1_out),
    .sel(aluctrl_1_x0));
  adder8b adder8b_1 (.A(A), .Cin(aluctrl_1_t), .B(xor_1_out), .Overflow(out_4), .S(adder8b_1_s));
  Multiplexer #(.width(8), .enable("false")) multiplexer_2 (
    .in0(adder8b_1_s), .in1(multiplexer_1_out), .out(out_5), .sel(aluctrl_1_y));
  // Probe on out_5
endmodule

module aluctrl (
  input  [3:0] in_1,
  output T,
  output X1,
  output X0,
  output Y
);

  or or_1 (T, in_1[2], in_1[3]);

  assign X0 = in_1[1];
  assign X1 = in_1[2];
  assign Y = in_1[3];
endmodule

module test (
);

  // MIPSProgramROM mipsprogramrom_1: pin names not known
  // MIPS_RAM mips_ram_1: pin names not known
  // RegisterFile registerfile_1: pin names not known
  // Mips_ALU mips_alu_1: pin names not known
endmodule

module test1 (
  input  in_1,
  input  R,
  output out_3,
  output out_4,
  output out_5
);

  wire clock_1_out, mainctrl_1_extop, mainctrl_1_ld, mainctrl_1_st, mainctrl_1_wen, nor_1_out,
       registerfile_1_p3, registerfile_1_p7;
  wire [1:0] register_1_q;
  wire [3:0] functalu_1_a0, multiplexer_4_out, opcodealu_1_a0;
  wire [4:0] multiplexer_2_out;
  wire [29:0] register_1_q_2;
  wire [31:0] extender_1_out_3, mips_alu_1_p5, mips_ram_1_p7, mipsprogramrom_1_p1, multiplexer_1_out,
       multiplexer_3_out, registerfile_1_p8;
  wire [31:2] incrementer_1_p2;

  Clock clock_1 (.out(clock_1_out));
  Register #(.width(32), .trigger("falling")) register_1 (
    .D({incrementer_1_p2, 2'b00}), .en(1'b1), .clk(clock_1_out), .Q({register_1_q_2, register_1_q}), .clr(R));
  // Incrementer #(.width(30)) incrementer_1: pin names not known; wires that end beside it: register_1_q_2, incrementer_1_p2, {register_1_q_2, register_1_q}
  // MIPSProgramROM mipsprogramrom_1: pin names not known; wires that end beside it: mipsprogramrom_1_p1
  Multiplexer #(.width(32), .enable("false")) multiplexer_1 (
    .in0(mips_alu_1_p5), .in1(mips_ram_1_p7), .out(multiplexer_1_out), .sel(mainctrl_1_ld));
  Multiplexer #(.width(5), .enable("false")) multiplexer_2 (
    .in0(mipsprogramrom_1_p1[20:16]), .in1(mipsprogramrom_1_p1[15:11]), .out(multiplexer_2_out),
    .sel(nor_1_out));
  nor nor_1 (nor_1_out, mipsprogramrom_1_p1[26], mipsprogramrom_1_p1[27], mipsprogramrom_1_p1[28], mipsprogramrom_1_p1[29], mipsprogramrom_1_p1[30], mipsprogramrom_1_p1[31]);
  // RegisterFile #(.trigger("falling")) registerfile_1: pin names not known; wires that end beside it: multiplexer_1_out, clock_1_out, registerfile_1_p3, multiplexer_2_out, mipsprogramrom_1_p1[25:21], mipsprogramrom_1_p1[20:16], registerfile_1_p7, registerfile_1_p8
  or or_1 (registerfile_1_p3, nor_1_out, mainctrl_1_wen);
  mainCtrl mainctrl_1 (
    .op5(mipsprogramrom_1_p1[26]), .op4(mipsprogramrom_1_p1[27]), .op3(mipsprogramrom_1_p1[28]),
    .op2(mipsprogramrom_1_p1[29]), .op1(mipsprogramrom_1_p1[30]), .op0(mipsprogramrom_1_p1[31]),
    .WEn(mainctrl_1_wen), .st(mainctrl_1_st), .ld(mainctrl_1_ld), .beq(out_3), .bne(out_4), .j(out_5),
    .ExtOp(mainctrl_1_extop));
  opcodeALU opcodealu_1 (
    .op5(mipsprogramrom_1_p1[26]), .op4(mipsprogramrom_1_p1[27]), .op3(mipsprogramrom_1_p1[28]),
    .op2(mipsprogramrom_1_p1[29]), .op1(mipsprogramrom_1_p1[30]), .op0(mipsprogramrom_1_p1[31]),
    .a3(opcodealu_1_a0[3]), .a2(opcodealu_1_a0[2]), .a1(opcodealu_1_a0[1]), .a0(opcodealu_1_a0[0]));
  functAlu functalu_1 (
    .f5(mipsprogramrom_1_p1[5]), .f4(mipsprogramrom_1_p1[4]), .f3(mipsprogramrom_1_p1[3]),
    .f2(mipsprogramrom_1_p1[2]), .f1(mipsprogramrom_1_p1[1]), .f0(mipsprogramrom_1_p1[0]),
    .a3(functalu_1_a0[3]), .a2(functalu_1_a0[2]), .a1(functalu_1_a0[1]), .a0(functalu_1_a0[0]));
  extender extender_1 (.ExtOP(mainctrl_1_extop), .Din(mipsprogramrom_1_p1[15:0]), .out_3(extender_1_out_3));
  Multiplexer #(.width(32), .enable("false")) multiplexer_3 (
    .in0(registerfile_1_p8), .in1(extender_1_out_3), .out(multiplexer_3_out), .sel(nor_1_out));
  Multiplexer #(.width(4), .enable("false")) multiplexer_4 (
    .in0(functalu_1_a0), .in1(opcodealu_1_a0), .out(multiplexer_4_out), .sel(nor_1_out));
  // Mips_ALU mips_alu_1: pin names not known; wires that end beside it: registerfile_1_p7, multiplexer_3_out, multiplexer_4_out, mipsprogramrom_1_p1[10:6], mips_alu_1_p5
  // MIPS_RAM mips_ram_1: pin names not known; wires that end beside it: mips_alu_1_p5[19:0], registerfile_1_p7, mainctrl_1_st, clock_1_out, mainctrl_1_ld, in_1, mips_ram_1_p7

  // Notes on the sheet:
  //   contents of mipsprogramrom_1 (hex, n*v repeats v):
  //   funkcija: subu $2, $4, $5 jr $31  main: addiu $8, $0, 4 ori $9, $0, 0xabcd sll $9, $9, 16 ori $9,
  //   $9, 0x1234 sw $9, 0($8) sw $9, 4($8) ori $10, $0, 4 addu $12, $8, $10 lw $13, 0($12) addu $5, $0,
  //   $13 bne   $5, $0, razlicito addiu $4, $5, -8 j     krajif razlicito: addiu $4, $5, 8 krajif:  jal
  //   funkcija sw $2, 8($8)  # Nakon izvrsenja programa u RAM memoriji bi trebalo da budu podaci: # adresa
  //   0: 0xabcd1234 # adresa 4: 0xabcd1234 # adresa 8: 0x00000008 # Ako je na adresi 8 vrijednost
  //   0xfffffff8 onda branch ne radi kako bi trebalo
endmodule

module functAlu (
  input  f5,
  input  f4,
  input  f3,
  input  f2,
  input  f1,
  input  f0,
  output a3,
  output a2,
  output a1,
  output a0
);

  wire not_1_out;

  and and_1 (a1, f5, f0);
  not not_1 (not_1_out, f5);
  and and_2 (a0, not_1_out, f0);

  assign a2 = f1;
  assign a3 = f2;
endmodule

module mainCtrl (
  input  op5,
  input  op4,
  input  op3,
  input  op2,
  input  op1,
  input  op0,
  output WEn,
  output st,
  output ld,
  output beq,
  output bne,
  output j,
  output ExtOp
);

  wire and_2_out, and_3_out, and_7_out, and_8_out, not_1_out, not_2_out, not_3_out, not_4_out, not_5_out,
       not_6_out, not_7_out, not_8_out, not_9_out;

  not not_1 (not_1_out, op3);
  not not_2 (not_2_out, op5);
  and and_1 (st, op5, op3);
  not not_3 (not_3_out, op3);
  not not_4 (not_4_out, op3);
  not not_5 (not_5_out, op0);
  not not_6 (not_6_out, op3);
  not not_7 (not_7_out, op1);
  not not_8 (not_8_out, op2);
  not not_9 (not_9_out, op3);
  and and_2 (and_2_out, not_1_out, op1);
  and and_3 (and_3_out, not_2_out, op3);
  and and_4 (ld, op5, not_3_out);
  and and_5 (beq, not_4_out, op2, not_5_out);
  and and_6 (bne, not_6_out, not_7_out, op0);
  and and_7 (and_7_out, not_8_out, op0);
  and and_8 (and_8_out, not_9_out, op2);
  or or_1 (WEn, and_2_out, and_3_out);
  or or_2 (ExtOp, and_7_out, and_8_out);

  assign j = 1'b0;
endmodule

module opcodeALU (
  input  op5,
  input  op4,
  input  op3,
  input  op2,
  input  op1,
  input  op0,
  output a3,
  output a2,
  output a1,
  output a0
);

  wire and_2_out, and_3_out, not_1_out, not_2_out, not_3_out, not_4_out;

  and and_1 (a3, op3, op2);
  not not_1 (not_1_out, op3);
  not not_2 (not_2_out, op1);
  not not_3 (not_3_out, op0);
  not not_4 (not_4_out, op3);
  and and_2 (and_2_out, not_1_out, not_2_out);
  and and_3 (and_3_out, op1, not_3_out);
  or or_1 (a1, not_4_out, op0);
  or or_2 (a2, and_2_out, and_3_out);

  assign a0 = 1'b0;
endmodule

module extender (
  input  ExtOP,
  input  [15:0] Din,
  output [31:0] out_3
);

  and and_1 (out_3[31], ExtOP, Din[15]);

  assign out_3[30:0] = {{15{out_3[31]}}, Din};
endmodule
