// Logisim project adel_sehic_20039.circ as structural Verilog: 10 circuits, main circuit main
module main (
  input  ResetPC
);

  wire aluctrl_1_jr, c, mctrl2_1_alusrc, mctrl2_1_beq, mctrl2_1_bne, mctrl2_1_ext, mctrl2_1_j, mctrl2_1_jal,
       mctrl2_1_memr, mctrl2_1_memreg, mctrl2_1_memw, mctrl2_1_rd, mctrl2_1_wen, registerfile_1_p7;
  wire [3:0] aluctrl_1_ctrl;
  wire [4:0] multiplexer_1_out, multiplexer_3_out, sh;
  wire [23:0] mips_alu_1_p5;
  wire [31:0] extender_1_d, mips_ram_1_p6, mipsprogramrom_1_p2, multiplexer_2_out, multiplexer_4_out,
       multiplexer_5_out, npc, pc, pcn, registerfile_1_p8;
  wire [31:24] mips_alu_1_p5_2;

  Clock clock_1 (.out(c));
  Register #(.width(32)) u_PC (.D(npc), .en(1'b1), .clk(c), .Q(pc), .clr(ResetPC));
  // MIPSProgramROM mipsprogramrom_1: pin names not known; wires that end beside it: pc, {mipsprogramrom_1_p2[31:11], sh, mipsprogramrom_1_p2[5:0]}
  extender extender_1 (
    .D(extender_1_d), .s({mipsprogramrom_1_p2[15:11], sh, mipsprogramrom_1_p2[5:0]}), .imm(mctrl2_1_ext));
  aluctrl aluctrl_1 (
    .funct(mipsprogramrom_1_p2[5:0]), .opcode(mipsprogramrom_1_p2[31:26]), .ctrl(aluctrl_1_ctrl),
    .jr(aluctrl_1_jr));
  mctrl2 mctrl2_1 (
    .bne(mctrl2_1_bne), .aluSrc(mctrl2_1_alusrc), .wen(mctrl2_1_wen), .rd(mctrl2_1_rd),
    .op1(mipsprogramrom_1_p2[27]), .op3(mipsprogramrom_1_p2[29]), .op5(mipsprogramrom_1_p2[31]),
    .op4(mipsprogramrom_1_p2[30]), .op2(mipsprogramrom_1_p2[28]), .op0(mipsprogramrom_1_p2[26]),
    .jal(mctrl2_1_jal), .ext(mctrl2_1_ext), .beq(mctrl2_1_beq), .j(mctrl2_1_j), .memR(mctrl2_1_memr),
    .memW(mctrl2_1_memw), .memReg(mctrl2_1_memreg));
  Multiplexer #(.width(5), .enable("false")) multiplexer_1 (
    .in0(mipsprogramrom_1_p2[20:16]), .in1(mipsprogramrom_1_p2[15:11]), .out(multiplexer_1_out),
    .sel(mctrl2_1_rd));
  Multiplexer #(.width(32), .enable("false")) multiplexer_2 (
    .in0(multiplexer_5_out), .in1(pcn), .out(multiplexer_2_out), .sel(mctrl2_1_jal));
  Multiplexer #(.width(5), .enable("false")) multiplexer_3 (
    .in0(multiplexer_1_out), .in1({5{1'b1}}), .out(multiplexer_3_out), .sel(mctrl2_1_jal));
  nextPC nextpc_1 (
    .imm({mipsprogramrom_1_p2[25:11], sh, mipsprogramrom_1_p2[5:0]}), .bne(mctrl2_1_bne), .j(mctrl2_1_j),
    .nextPC(npc), .beq(mctrl2_1_beq), .zer0({mips_alu_1_p5_2, mips_alu_1_p5}), .PC(pc), .pc1(pcn),
    .jr(aluctrl_1_jr));
  // RegisterFile registerfile_1: pin names not known; wires that end beside it: multiplexer_2_out, c, mctrl2_1_wen, multiplexer_3_out, mipsprogramrom_1_p2[25:21], mipsprogramrom_1_p2[20:16], registerfile_1_p7, registerfile_1_p8
  Multiplexer #(.width(32), .enable("false")) multiplexer_4 (
    .in0(registerfile_1_p8), .in1(extender_1_d), .out(multiplexer_4_out), .sel(mctrl2_1_alusrc));
  Multiplexer #(.width(32), .enable("false")) multiplexer_5 (
    .in0({mips_alu_1_p5_2, mips_alu_1_p5}), .in1(mips_ram_1_p6), .out(multiplexer_5_out), .sel(mctrl2_1_memr));
  // Mips_ALU mips_alu_1: pin names not known; wires that end beside it: registerfile_1_p7, multiplexer_4_out, aluctrl_1_ctrl, sh, {mips_alu_1_p5_2, mips_alu_1_p5}
  // MIPS_RAM #(.addrWidth(24)) mips_ram_1: pin names not known; wires that end beside it: mips_alu_1_p5, registerfile_1_p8, mctrl2_1_memw, c, mctrl2_1_memreg, mips_ram_1_p6

  // Notes on the sheet:
  //   contents of mipsprogramrom_1 (hex, n*v repeats v):
  //   funkcija: subu $2, $4, $5 jr $31  main: addiu $8, $0, 4 ori $9, $0, 0xabcd sll $9, $9, 16 ori $9,
  //   $9, 0x1234 sw $9, 0($8) sw $9, 4($8) ori $10, $0, 4 addu $12, $8, $10 lw $13, 0($12) addu $5, $0,
  //   $13 bne   $5, $0, razlicito addiu $4, $5, -8 j     krajif razlicito: addiu $4, $5, 8 krajif:  jal
  //   funkcija sw $2, 8($8) # Nakon izvrsenja programa u RAM memoriji bi trebalo da budu podaci: # adresa
  //   0: 0xabcd1234 # adresa 4: 0xabcd1234 # adresa 8: 0x00000008 # Ako je na adresi 8 vrijednost
  //   0xfffffff8 onda branch ne radi kako bi trebalo
  //   funct
  //   shamt
  //   rd
  //   rt
  //   rs
  //   opcode
endmodule

module extender (
  input  imm,
  input  [15:0] s,
  output [31:0] D
);

  and and_1 (D[31], imm, s[15]);

  assign D[30:0] = {{15{D[31]}}, s};
endmodule

module zero (
  input  [31:0] D,
  output Z
);

  nor nor_1 (Z, D[0], D[1], D[2], D[3], D[4], D[5], D[6], D[7], D[8], D[9], D[10], D[11], D[12], D[13], D[14], D[15], D[16], D[17], D[18], D[19], D[20], D[21], D[22], D[23], D[24], D[25], D[26], D[27], D[28], D[29], D[30], D[31]);
endmodule

module aluFunct (
  input  f0,
  input  f1,
  input  f2,
  input  f3,
  input  f4,
  input  f5,
  output o0,
  output o1,
  output o2,
  output o3
);

  wire and_1_out, and_2_out, and_3_out, not_1_out, not_2_out, not_3_out, not_4_out, not_5_out, not_6_out,
       not_7_out, not_8_out, not_9_out, not_10_out;

  not not_1 (not_1_out, f0);
  not not_2 (not_2_out, f1);
  not not_3 (not_3_out, f4);
  not not_4 (not_4_out, f5);
  not not_5 (not_5_out, f0);
  not not_6 (not_6_out, f1);
  not not_7 (not_7_out, f3);
  not not_8 (not_8_out, f4);
  not not_9 (not_9_out, f5);
  not not_10 (not_10_out, f0);
  and and_1 (and_1_out, not_1_out, not_2_out, f2, not_3_out, not_4_out);
  and and_2 (and_2_out, not_5_out, not_6_out, f2, not_7_out, not_8_out, not_9_out);
  and and_3 (and_3_out, f0, f5);
  and and_4 (o3, not_10_out, f5);
  or or_1 (o0, f3, and_1_out);
  or or_2 (o2, and_2_out, and_3_out);

  assign o1 = f4;
endmodule

module aluOp (
  input  op0,
  input  op1,
  input  op2,
  input  op3,
  input  op4,
  input  op5,
  output o0,
  output o1,
  output o2,
  output o3
);

  wire and_2_out, and_3_out, not_1_out, not_2_out, not_3_out, not_4_out;

  and and_1 (o0, op2, op3);
  not not_1 (not_1_out, op2);
  not not_2 (not_2_out, op4);
  not not_3 (not_3_out, op5);
  not not_4 (not_4_out, op2);
  and and_2 (and_2_out, not_1_out, not_2_out);
  and and_3 (and_3_out, op4, not_3_out);
  or or_1 (o2, not_4_out, op5);
  or or_2 (o1, and_2_out, and_3_out);

  assign o3 = 1'b0;
endmodule

module aluctrl (
  input  [5:0] opcode,
  input  [5:0] funct,
  output [3:0] ctrl,
  output jr
);

  wire nor_1_out;
  wire [3:0] alufunct_1_o3, aluop_1_o3;

  nor nor_1 (nor_1_out, opcode[5], opcode[4], opcode[3], opcode[2], opcode[1], opcode[0]);
  aluOp aluop_1 (
    .op0(opcode[5]), .op1(opcode[4]), .op2(opcode[3]), .op3(opcode[2]), .op4(opcode[1]), .op5(opcode[0]),
    .o0(aluop_1_o3[3]), .o1(aluop_1_o3[2]), .o2(aluop_1_o3[1]), .o3(aluop_1_o3[0]));
  aluFunct alufunct_1 (
    .f0(funct[5]), .f1(funct[4]), .f2(funct[3]), .f3(funct[2]), .f4(funct[1]), .f5(funct[0]),
    .o0(alufunct_1_o3[3]), .o1(alufunct_1_o3[2]), .o2(alufunct_1_o3[1]), .o3(alufunct_1_o3[0]));
  Multiplexer #(.width(4), .enable("false")) multiplexer_1 (
    .in0(aluop_1_o3), .in1(alufunct_1_o3), .out(ctrl), .sel(nor_1_out));
  and and_1 (jr, nor_1_out, ~funct[5], ~funct[4], funct[3], ~funct[2], ~funct[1], ~funct[0]);  // AND_Gate
endmodule

module nextPC (
  input  jr,
  input  [31:0] PC,
  input  beq,
  input  bne,
  input  [25:0] imm,
  input  j,
  input  [31:0] zer0,
  output [31:0] nextPC,
  output [31:0] pc1
);

  wire and_1_out, and_2_out, or_1_out, zero_1_z;
  wire [29:0] adder_1_out, bit_extender_1_out, multiplexer_1_out, multiplexer_2_out;

  // Incrementer #(.width(30)) incrementer_1: pin names not known; wires that end beside it: PC[31:2], pc1[31:2]
  assign bit_extender_1_out = {{14{imm[15]}}, imm[15:0]};  // Bit_Extender bit_extender_1
  Adder #(.width(30)) adder_1 (.a(pc1[31:2]), .b(bit_extender_1_out), .out(adder_1_out));  // open: cin, cout
  Multiplexer #(.width(30), .enable("false")) multiplexer_1 (
    .in0(adder_1_out), .in1({pc1[31:28], imm}), .out(multiplexer_1_out), .sel(j));
  Multiplexer #(.width(30), .enable("false")) multiplexer_2 (
    .in0(pc1[31:2]), .in1(multiplexer_1_out), .out(multiplexer_2_out), .sel(or_1_out));
  Multiplexer #(.width(32), .enable("false")) multiplexer_3 (
    .in0({multiplexer_2_out, 2'b00}), .in1(zer0), .out(nextPC), .sel(jr));
  and and_1 (and_1_out, ~zero_1_z, bne);  // AND_Gate
  zero zero_1 (.Z(zero_1_z), .D(zer0));
  or or_1 (or_1_out, and_1_out, j, and_2_out);
  and and_2 (and_2_out, zero_1_z, beq);

  assign pc1[1:0] = 2'b00;
endmodule

module mctrl (
  input  op5,
  input  op4,
  input  op3,
  input  op2,
  input  op1,
  input  op0,
  output rd,
  output jal,
  output wen,
  output ext,
  output aluSrc,
  output beq,
  output bne,
  output j,
  output memR,
  output memW,
  output memReg
);

  wire and_2_out, and_3_out, and_4_out, and_5_out, and_6_out, and_7_out, and_8_out, and_9_out, and_10_out,
       and_11_out, and_12_out, and_13_out, and_14_out, and_15_out, and_16_out, and_17_out, and_18_out,
       and_19_out, and_20_out, and_21_out, and_22_out, and_23_out, and_24_out, and_25_out, and_26_out,
       and_27_out, and_28_out, and_29_out, and_30_out, and_31_out, and_32_out, and_33_out, and_34_out,
       and_35_out, and_36_out, and_37_out, not_1_out, not_2_out, not_3_out, not_4_out, not_5_out, not_6_out,
       not_7_out, not_8_out, not_9_out, not_10_out, not_11_out, not_12_out, not_13_out, not_14_out,
       not_15_out, not_16_out, not_17_out, not_18_out, not_19_out, not_20_out, not_21_out, not_22_out,
       not_23_out, not_24_out, not_25_out, not_26_out, not_27_out, not_28_out, not_29_out, not_30_out,
       not_31_out, not_32_out, not_33_out, not_34_out, not_35_out, not_36_out, not_37_out, not_38_out,
       not_39_out, not_40_out, not_41_out, not_42_out, not_43_out, not_44_out, not_45_out, not_46_out,
       not_47_out, not_48_out, not_49_out, not_50_out, not_51_out, not_52_out, not_53_out, not_54_out,
       not_55_out, not_56_out, not_57_out, not_58_out, not_59_out, not_60_out, not_61_out, not_62_out,
       not_63_out, not_64_out, not_65_out, not_66_out, not_67_out, not_68_out, not_69_out, not_70_out,
       not_71_out, not_72_out, not_73_out, not_74_out, not_75_out, not_76_out, not_77_out, not_78_out,
       not_79_out, not_80_out, not_81_out, not_82_out;

  not not_1 (not_1_out, op5);
  not not_2 (not_2_out, op4);
  not not_3 (not_3_out, op3);
  not not_4 (not_4_out, op2);
  and and_1 (jal, not_1_out, not_2_out, not_3_out, not_4_out, op1, op0);
  not not_5 (not_5_out, op5);
  not not_6 (not_6_out, op4);
  not not_7 (not_7_out, op3);
  not not_8 (not_8_out, op1);
  not not_9 (not_9_out, op5);
  not not_10 (not_10_out, op3);
  not not_11 (not_11_out, op2);
  not not_12 (not_12_out, op3);
  not not_13 (not_13_out, op2);
  not not_14 (not_14_out, op1);
  not not_15 (not_15_out, op3);
  not not_16 (not_16_out, op2);
  not not_17 (not_17_out, op0);
  not not_18 (not_18_out, op3);
  not not_19 (not_19_out, op2);
  not not_20 (not_20_out, op2);
  not not_21 (not_21_out, op1);
  not not_22 (not_22_out, op0);
  not not_23 (not_23_out, op5);
  not not_24 (not_24_out, op4);
  not not_25 (not_25_out, op4);
  not not_26 (not_26_out, op1);
  not not_27 (not_27_out, op4);
  not not_28 (not_28_out, op0);
  not not_29 (not_29_out, op4);
  not not_30 (not_30_out, op3);
  not not_31 (not_31_out, op1);
  not not_32 (not_32_out, op0);
  not not_33 (not_33_out, op1);
  not not_34 (not_34_out, op0);
  not not_35 (not_35_out, op3);
  not not_36 (not_36_out, op2);
  not not_37 (not_37_out, op2);
  not not_38 (not_38_out, op0);
  not not_39 (not_39_out, op0);
  not not_40 (not_40_out, op5);
  not not_41 (not_41_out, op4);
  not not_42 (not_42_out, op3);
  not not_43 (not_43_out, op1);
  not not_44 (not_44_out, op0);
  not not_45 (not_45_out, op0);
  not not_46 (not_46_out, op4);
  not not_47 (not_47_out, op2);
  or or_1 (aluSrc, op1, op3);
  not not_48 (not_48_out, op5);
  not not_49 (not_49_out, op3);
  not not_50 (not_50_out, op2);
  not not_51 (not_51_out, op3);
  not not_52 (not_52_out, op2);
  not not_53 (not_53_out, op1);
  not not_54 (not_54_out, op5);
  not not_55 (not_55_out, op4);
  not not_56 (not_56_out, op3);
  not not_57 (not_57_out, op1);
  not not_58 (not_58_out, op0);
  not not_59 (not_59_out, op3);
  not not_60 (not_60_out, op2);
  not not_61 (not_61_out, op3);
  not not_62 (not_62_out, op1);
  not not_63 (not_63_out, op3);
  not not_64 (not_64_out, op1);
  not not_65 (not_65_out, op3);
  not not_66 (not_66_out, op1);
  not not_67 (not_67_out, op5);
  not not_68 (not_68_out, op3);
  not not_69 (not_69_out, op2);
  not not_70 (not_70_out, op3);
  not not_71 (not_71_out, op2);
  not not_72 (not_72_out, op0);
  not not_73 (not_73_out, op3);
  not not_74 (not_74_out, op2);
  not not_75 (not_75_out, op3);
  not not_76 (not_76_out, op3);
  not not_77 (not_77_out, op2);
  not not_78 (not_78_out, op2);
  not not_79 (not_79_out, op5);
  not not_80 (not_80_out, op3);
  not not_81 (not_81_out, op1);
  not not_82 (not_82_out, op2);
  and and_2 (and_2_out, not_5_out, not_6_out, not_7_out, not_8_out);
  and and_3 (and_3_out, not_9_out, not_10_out, not_11_out);
  and and_4 (and_4_out, not_12_out, not_13_out, not_14_out);
  and and_5 (and_5_out, not_15_out, not_16_out, not_17_out);
  and and_6 (and_6_out, op4, not_18_out, not_19_out);
  and and_7 (and_7_out, not_20_out, not_21_out, not_22_out);
  and and_8 (and_8_out, not_23_out, not_24_out, op3);
  and and_9 (and_9_out, not_25_out, op3, not_26_out);
  and and_10 (and_10_out, not_27_out, op3, not_28_out);
  and and_11 (and_11_out, not_29_out, op3, op2);
  and and_12 (and_12_out, op4, not_30_out);
  and and_13 (and_13_out, op4, not_31_out, not_32_out);
  and and_14 (and_14_out, op5, not_33_out, not_34_out);
  and and_15 (and_15_out, op5, not_35_out, not_36_out, op1, op0);
  and and_16 (and_16_out, not_37_out, not_38_out);
  and and_17 (and_17_out, op1, not_39_out);
  and and_18 (and_18_out, not_40_out, not_41_out, not_42_out, op2, not_43_out);
  and and_19 (and_19_out, op4, not_44_out);
  and and_20 (and_20_out, op5, not_45_out);
  and and_21 (and_21_out, op5, not_46_out, not_47_out, op1);
  and and_22 (and_22_out, not_48_out, not_49_out, not_50_out, op0);
  and and_23 (and_23_out, not_51_out, not_52_out, not_53_out, op0);
  and and_24 (and_24_out, not_54_out, not_55_out, not_56_out, op2, not_57_out, not_58_out);
  and and_25 (and_25_out, op4, not_59_out, not_60_out, op0);
  and and_26 (and_26_out, not_61_out, op2, not_62_out, op0);
  and and_27 (and_27_out, op4, not_63_out, op2, not_64_out);
  or or_2 (bne, and_26_out, and_27_out, and_28_out);
  and and_28 (and_28_out, op5, not_65_out, op2, not_66_out);
  and and_29 (and_29_out, not_67_out, not_68_out, not_69_out, op1);
  or or_3 (j, and_29_out, and_30_out, and_31_out);
  and and_30 (and_30_out, not_70_out, not_71_out, not_72_out, op1);
  and and_31 (and_31_out, op4, not_73_out, not_74_out, op1);
  and and_32 (and_32_out, op4, not_75_out);
  or or_4 (memR, and_32_out, and_33_out);
  and and_33 (and_33_out, op5, not_76_out, not_77_out, op0, op1);
  and and_34 (and_34_out, op4, op3);
  or or_5 (memW, and_34_out, and_35_out);
  and and_35 (and_35_out, op5, op3, not_78_out, op0, op1);
  and and_36 (and_36_out, not_79_out, not_80_out, op2, not_81_out);
  or or_6 (memReg, and_36_out, op4, and_37_out);
  and and_37 (and_37_out, op5, not_82_out, op1, op0);
  or or_7 (rd, and_2_out, and_3_out, and_4_out, and_5_out, and_6_out);
  or or_8 (wen, and_7_out, and_8_out, and_9_out, and_10_out, and_11_out, and_12_out, and_13_out, and_14_out, and_15_out);
  or or_9 (ext, and_16_out, and_17_out, and_18_out, and_19_out, and_20_out, and_21_out);
  or or_10 (beq, and_22_out, and_23_out, and_24_out, and_25_out);
endmodule

module jal (
  input  op5,
  input  op4,
  input  op3,
  input  op2,
  input  op1,
  input  op0,
  output jal
);

  wire not_1_out, not_2_out, not_3_out, not_4_out;

  not not_1 (not_1_out, op5);
  not not_2 (not_2_out, op4);
  not not_3 (not_3_out, op3);
  not not_4 (not_4_out, op2);
  and and_1 (jal, not_1_out, not_2_out, not_3_out, not_4_out, op1, op0);
endmodule

module mctrl2 (
  input  op5,
  input  op4,
  input  op3,
  input  op2,
  input  op1,
  input  op0,
  output rd,
  output jal,
  output wen,
  output ext,
  output aluSrc,
  output beq,
  output bne,
  output j,
  output memR,
  output memW,
  output memReg
);

  wire and_1_out, and_2_out, and_3_out, and_4_out, and_5_out, and_7_out, and_8_out, and_9_out, and_10_out,
       and_11_out, and_12_out, and_13_out, and_14_out, and_15_out, and_16_out, and_17_out, and_18_out,
       and_19_out, and_20_out, and_21_out, and_22_out, and_23_out, and_24_out, and_25_out, and_26_out,
       and_27_out, and_28_out, and_29_out, and_30_out, and_31_out, and_32_out, and_33_out, and_34_out,
       and_35_out, and_36_out, not_1_out, not_2_out, not_3_out, not_4_out, not_5_out, not_6_out, not_7_out,
       not_8_out, not_9_out, not_10_out, not_11_out, not_12_out, not_13_out, not_14_out, not_15_out,
       not_16_out, not_17_out, not_18_out, not_19_out, not_20_out, not_21_out, not_22_out, not_23_out,
       not_24_out, not_25_out, not_26_out, not_27_out, not_28_out, not_29_out, not_30_out, not_31_out,
       not_32_out, not_33_out, not_34_out, not_35_out, not_36_out, not_37_out, not_38_out, not_39_out,
       not_40_out, not_41_out, not_42_out, not_43_out, not_44_out, not_45_out, not_46_out, not_47_out,
       not_48_out, not_49_out, not_50_out, not_51_out, not_52_out, not_53_out, not_54_out, not_55_out,
       not_56_out, not_57_out, not_58_out, not_59_out, not_60_out, not_61_out, not_62_out, not_63_out,
       not_64_out, not_65_out, not_66_out, not_67_out, not_68_out, not_69_out, not_70_out, not_71_out,
       not_72_out, not_73_out, not_74_out, not_75_out, not_76_out, not_77_out, not_78_out, not_79_out;

  not not_1 (not_1_out, op5);
  not not_2 (not_2_out, op4);
  not not_3 (not_3_out, op3);
  not not_4 (not_4_out, op1);
  not not_5 (not_5_out, op5);
  not not_6 (not_6_out, op3);
  not not_7 (not_7_out, op2);
  not not_8 (not_8_out, op3);
  not not_9 (not_9_out, op2);
  not not_10 (not_10_out, op1);
  not not_11 (not_11_out, op3);
  not not_12 (not_12_out, op2);
  not not_13 (not_13_out, op0);
  not not_14 (not_14_out, op3);
  not not_15 (not_15_out, op2);
  not not_16 (not_16_out, op5);
  not not_17 (not_17_out, op4);
  not not_18 (not_18_out, op3);
  not not_19 (not_19_out, op2);
  not not_20 (not_20_out, op2);
  not not_21 (not_21_out, op1);
  not not_22 (not_22_out, op0);
  not not_23 (not_23_out, op3);
  not not_24 (not_24_out, op2);
  not not_25 (not_25_out, op5);
  not not_26 (not_26_out, op4);
  not not_27 (not_27_out, op4);
  not not_28 (not_28_out, op1);
  not not_29 (not_29_out, op4);
  not not_30 (not_30_out, op0);
  not not_31 (not_31_out, op4);
  not not_32 (not_32_out, op3);
  not not_33 (not_33_out, op1);
  not not_34 (not_34_out, op0);
  not not_35 (not_35_out, op1);
  not not_36 (not_36_out, op0);
  not not_37 (not_37_out, op2);
  not not_38 (not_38_out, op0);
  not not_39 (not_39_out, op0);
  not not_40 (not_40_out, op5);
  not not_41 (not_41_out, op4);
  not not_42 (not_42_out, op3);
  not not_43 (not_43_out, op1);
  not not_44 (not_44_out, op0);
  not not_45 (not_45_out, op0);
  not not_46 (not_46_out, op4);
  not not_47 (not_47_out, op2);
  or or_1 (aluSrc, op1, op3);
  not not_48 (not_48_out, op3);
  not not_49 (not_49_out, op2);
  not not_50 (not_50_out, op1);
  not not_51 (not_51_out, op5);
  not not_52 (not_52_out, op4);
  not not_53 (not_53_out, op3);
  not not_54 (not_54_out, op1);
  not not_55 (not_55_out, op0);
  not not_56 (not_56_out, op3);
  not not_57 (not_57_out, op2);
  not not_58 (not_58_out, op3);
  not not_59 (not_59_out, op1);
  not not_60 (not_60_out, op3);
  not not_61 (not_61_out, op1);
  not not_62 (not_62_out, op3);
  not not_63 (not_63_out, op1);
  not not_64 (not_64_out, op5);
  not not_65 (not_65_out, op3);
  not not_66 (not_66_out, op2);
  not not_67 (not_67_out, op3);
  not not_68 (not_68_out, op2);
  not not_69 (not_69_out, op0);
  not not_70 (not_70_out, op3);
  not not_71 (not_71_out, op2);
  not not_72 (not_72_out, op3);
  not not_73 (not_73_out, op3);
  not not_74 (not_74_out, op2);
  not not_75 (not_75_out, op2);
  not not_76 (not_76_out, op5);
  not not_77 (not_77_out, op3);
  not not_78 (not_78_out, op1);
  not not_79 (not_79_out, op2);
  and and_1 (and_1_out, not_1_out, not_2_out, not_3_out, not_4_out);
  and and_2 (and_2_out, not_5_out, not_6_out, not_7_out);
  and and_3 (and_3_out, not_8_out, not_9_out, not_10_out);
  and and_4 (and_4_out, not_11_out, not_12_out, not_13_out);
  and and_5 (and_5_out, op4, not_14_out, not_15_out);
  and and_6 (jal, not_16_out, not_17_out, not_18_out, not_19_out, op1, op0);
  and and_7 (and_7_out, not_20_out, not_21_out, not_22_out);
  and and_8 (and_8_out, not_23_out, not_24_out, op1, op0);
  and and_9 (and_9_out, not_25_out, not_26_out, op3);
  and and_10 (and_10_out, not_27_out, op3, not_28_out);
  and and_11 (and_11_out, not_29_out, op3, not_30_out);
  and and_12 (and_12_out, not_31_out, op3, op2);
  and and_13 (and_13_out, op4, not_32_out);
  and and_14 (and_14_out, op4, not_33_out, not_34_out);
  and and_15 (and_15_out, op5, not_35_out, not_36_out);
  and and_16 (and_16_out, not_37_out, not_38_out);
  and and_17 (and_17_out, op1, not_39_out);
  and and_18 (and_18_out, not_40_out, not_41_out, not_42_out, op2, not_43_out);
  and and_19 (and_19_out, op4, not_44_out);
  and and_20 (and_20_out, op5, not_45_out);
  and and_21 (and_21_out, op5, not_46_out, not_47_out, op1);
  and and_22 (and_22_out, not_48_out, not_49_out, not_50_out, op0);
  and and_23 (and_23_out, not_51_out, not_52_out, not_53_out, op2, not_54_out, not_55_out);
  and and_24 (and_24_out, op4, not_56_out, not_57_out, op0);
  and and_25 (and_25_out, not_58_out, op2, not_59_out, op0);
  and and_26 (and_26_out, op4, not_60_out, op2, not_61_out);
  and and_27 (and_27_out, op5, not_62_out, op2, not_63_out);
  and and_28 (and_28_out, not_64_out, not_65_out, not_66_out, op1);
  and and_29 (and_29_out, not_67_out, not_68_out, op1, not_69_out);
  and and_30 (and_30_out, op4, not_70_out, not_71_out, op1);
  and and_31 (and_31_out, op4, not_72_out);
  and and_32 (and_32_out, op5, not_73_out, not_74_out, op0, op1);
  and and_33 (and_33_out, op4, op3);
  and and_34 (and_34_out, op5, op3, not_75_out, op0, op1);
  and and_35 (and_35_out, not_76_out, not_77_out, op2, not_78_out);
  and and_36 (and_36_out, op5, not_79_out, op1, op0);
  or or_2 (rd, and_1_out, and_2_out, and_3_out, and_4_out, and_5_out);
  or or_3 (wen, and_7_out, and_8_out, and_9_out, and_10_out, and_11_out, and_12_out, and_13_out, and_14_out, and_15_out);
  or or_4 (ext, and_16_out, and_17_out, and_18_out, and_19_out, and_20_out, and_21_out);
  or or_5 (beq, and_22_out, and_23_out, and_24_out);
  or or_6 (bne, and_25_out, and_26_out, and_27_out);
  or or_7 (j, and_28_out, and_29_out, and_30_out);
  or or_8 (memR, and_31_out, and_32_out);
  or or_9 (memW, and_33_out, and_34_out);
  or or_10 (memReg, and_35_out, op4, and_36_out);
endmodule
