// Logisim project mipsCpu.circ as structural Verilog: 8 circuits, main circuit main
module main (
  input  ResetPC
);

  wire c, mainctrl_1_alusrc, mainctrl_1_beq, mainctrl_1_bne, mainctrl_1_ext, mainctrl_1_j, mainctrl_1_memr,
       mainctrl_1_memreg, mainctrl_1_memw, mainctrl_1_rd, mainctrl_1_wen, registerfile_1_p7;
  wire [3:0] aluctrl_1_ctrl;
  wire [4:0] multiplexer_1_out, sh;
  wire [23:0] mips_alu_1_p5;
  wire [31:0] extender_1_d, mips_ram_1_p6, mipsprogramrom_1_p2, multiplexer_2_out, npc, pc,
       registerfile_1_p1, registerfile_1_p8;
  wire [31:24] mips_alu_1_p5_2;

  Clock clock_1 (.out(c));
  Register #(.width(32)) u_PC (.D(npc), .en(1'b1), .clk(c), .Q(pc), .clr(ResetPC));
  // MIPSProgramROM mipsprogramrom_1: pin names not known; wires that end beside it: pc, {mipsprogramrom_1_p2[31:11], sh, mipsprogramrom_1_p2[5:0]}
  extender extender_1 (
    .s({mipsprogramrom_1_p2[15:11], sh, mipsprogramrom_1_p2[5:0]}), .imm(mainctrl_1_ext), .D(extender_1_d));
  Multiplexer #(.width(5), .enable("false")) multiplexer_1 (
    .in0(mipsprogramrom_1_p2[20:16]), .in1(mipsprogramrom_1_p2[15:11]), .out(multiplexer_1_out),
    .sel(mainctrl_1_rd));
  aluctrl aluctrl_1 (.ctrl(aluctrl_1_ctrl), .opcode(mipsprogramrom_1_p2[31:26]), .funct(mipsprogramrom_1_p2[5:0]));
  mainCtrl mainctrl_1 (
    .j(mainctrl_1_j), .beq(mainctrl_1_beq), .ext(mainctrl_1_ext), .rd(mainctrl_1_rd),
    .op(mipsprogramrom_1_p2[31:26]), .wen(mainctrl_1_wen), .aluSrc(mainctrl_1_alusrc), .bne(mainctrl_1_bne),
    .memR(mainctrl_1_memr), .memW(mainctrl_1_memw), .memReg(mainctrl_1_memreg));
  nextPC nextpc_1 (
    .j(mainctrl_1_j), .bne(mainctrl_1_bne), .PC(pc), .beq(mainctrl_1_beq),
    .imm({mipsprogramrom_1_p2[25:11], sh, mipsprogramrom_1_p2[5:0]}),
    .zer0({mips_alu_1_p5_2, mips_alu_1_p5}), .nextPC(npc));
  // RegisterFile registerfile_1: pin names not known; wires that end beside it: registerfile_1_p1, c, mainctrl_1_wen, multiplexer_1_out, mipsprogramrom_1_p2[25:21], mipsprogramrom_1_p2[20:16], registerfile_1_p7, registerfile_1_p8
  Multiplexer #(.width(32), .enable("false")) multiplexer_2 (
    .in0(registerfile_1_p8), .in1(extender_1_d), .out(multiplexer_2_out), .sel(mainctrl_1_alusrc));
  Multiplexer #(.width(32), .enable("false")) multiplexer_3 (
    .in0({mips_alu_1_p5_2, mips_alu_1_p5}), .in1(mips_ram_1_p6), .out(registerfile_1_p1),
    .sel(mainctrl_1_memreg));
  // Mips_ALU mips_alu_1: pin names not known; wires that end beside it: registerfile_1_p7, multiplexer_2_out, aluctrl_1_ctrl, sh, {mips_alu_1_p5_2, mips_alu_1_p5}
  // MIPS_RAM #(.addrWidth(24)) mips_ram_1: pin names not known; wires that end beside it: mips_alu_1_p5, registerfile_1_p8, mainctrl_1_memw, c, mainctrl_1_memr, mips_ram_1_p6

  // Notes on the sheet:
  //   contents of mipsprogramrom_1 (hex, n*v repeats v):
  //   bne $t0,$t0,prvi addiu $t1,$0,1 addiu $t2,$0,4 prvi: bne $t0,$0,drugi addiu $t0,$t0,2 drugi: ori
  //   $t2,$t0,2 addiu $t1,$0,1 addiu $t2,$0,4 beq $0,$0,treci addiu $t1,$0,1 addiu $t2,$0,4 treci: j prvi
  //   funct
  //   shamt
  //   rd
  //   rt
  //   rs
  //   opcode
endmodule

module extender (
  input  imm,
  input  [15:0] s,
  output [31:0] D
);

  and and_1 (D[31], imm, s[15]);

  assign D[30:0] = {{15{D[31]}}, s};
endmodule

module mainCtrl (
  input  [5:0] op,
  output rd,
  output wen,
  output ext,
  output aluSrc,
  output beq,
  output bne,
  output j,
  output memR,
  output memW,
  output memReg
);

  wire and_1_out, and_2_out, and_3_out, and_4_out, and_5_out, and_6_out, and_7_out, and_8_out, and_9_out,
       and_10_out, and_11_out, and_12_out, and_13_out, and_14_out, and_15_out, and_16_out, and_17_out,
       and_18_out, and_19_out, and_20_out, and_21_out, and_22_out, and_23_out, and_24_out, and_25_out,
       and_26_out, and_27_out, and_28_out, and_29_out, and_30_out, and_31_out, and_32_out, and_33_out,
       and_34_out, and_35_out, and_36_out, not_1_out, not_2_out, not_3_out, not_4_out, not_5_out, not_6_out,
       not_7_out, not_8_out, not_9_out, not_10_out, not_11_out, not_12_out, not_13_out, not_14_out,
       not_15_out, not_16_out, not_17_out, not_18_out, not_19_out, not_20_out, not_21_out, not_22_out,
       not_23_out, not_24_out, not_25_out, not_26_out, not_27_out, not_28_out, not_29_out, not_30_out,
       not_31_out, not_32_out, not_33_out, not_34_out, not_35_out, not_36_out, not_37_out, not_38_out,
       not_39_out, not_40_out, not_41_out, not_42_out, not_43_out, not_44_out, not_45_out, not_46_out,
       not_47_out, not_48_out, not_49_out, not_50_out, not_51_out, not_52_out, not_53_out, not_54_out,
       not_55_out, not_56_out, not_57_out, not_58_out, not_59_out, not_60_out, not_61_out, not_62_out,
       not_63_out, not_64_out, not_65_out, not_66_out, not_67_out, not_68_out, not_69_out, not_70_out,
       not_71_out, not_72_out, not_73_out, not_74_out, not_75_out, not_76_out, not_77_out, not_78_out;

  not not_1 (not_1_out, op[5]);
  not not_2 (not_2_out, op[4]);
  not not_3 (not_3_out, op[3]);
  not not_4 (not_4_out, op[1]);
  not not_5 (not_5_out, op[5]);
  not not_6 (not_6_out, op[3]);
  not not_7 (not_7_out, op[2]);
  not not_8 (not_8_out, op[3]);
  not not_9 (not_9_out, op[2]);
  not not_10 (not_10_out, op[1]);
  not not_11 (not_11_out, op[3]);
  not not_12 (not_12_out, op[2]);
  not not_13 (not_13_out, op[0]);
  not not_14 (not_14_out, op[3]);
  not not_15 (not_15_out, op[2]);
  not not_16 (not_16_out, op[2]);
  not not_17 (not_17_out, op[1]);
  not not_18 (not_18_out, op[0]);
  not not_19 (not_19_out, op[5]);
  not not_20 (not_20_out, op[4]);
  not not_21 (not_21_out, op[4]);
  not not_22 (not_22_out, op[1]);
  not not_23 (not_23_out, op[4]);
  not not_24 (not_24_out, op[0]);
  not not_25 (not_25_out, op[4]);
  not not_26 (not_26_out, op[3]);
  not not_27 (not_27_out, op[1]);
  not not_28 (not_28_out, op[0]);
  not not_29 (not_29_out, op[1]);
  not not_30 (not_30_out, op[0]);
  not not_31 (not_31_out, op[3]);
  not not_32 (not_32_out, op[2]);
  not not_33 (not_33_out, op[2]);
  not not_34 (not_34_out, op[0]);
  not not_35 (not_35_out, op[0]);
  not not_36 (not_36_out, op[5]);
  not not_37 (not_37_out, op[4]);
  not not_38 (not_38_out, op[3]);
  not not_39 (not_39_out, op[1]);
  not not_40 (not_40_out, op[0]);
  not not_41 (not_41_out, op[0]);
  not not_42 (not_42_out, op[4]);
  not not_43 (not_43_out, op[2]);
  or or_1 (aluSrc, op[1], op[3]);
  not not_44 (not_44_out, op[5]);
  not not_45 (not_45_out, op[3]);
  not not_46 (not_46_out, op[2]);
  not not_47 (not_47_out, op[3]);
  not not_48 (not_48_out, op[2]);
  not not_49 (not_49_out, op[1]);
  not not_50 (not_50_out, op[5]);
  not not_51 (not_51_out, op[4]);
  not not_52 (not_52_out, op[3]);
  not not_53 (not_53_out, op[1]);
  not not_54 (not_54_out, op[0]);
  not not_55 (not_55_out, op[3]);
  not not_56 (not_56_out, op[2]);
  not not_57 (not_57_out, op[3]);
  not not_58 (not_58_out, op[1]);
  not not_59 (not_59_out, op[3]);
  not not_60 (not_60_out, op[1]);
  not not_61 (not_61_out, op[3]);
  not not_62 (not_62_out, op[1]);
  not not_63 (not_63_out, op[5]);
  not not_64 (not_64_out, op[3]);
  not not_65 (not_65_out, op[2]);
  not not_66 (not_66_out, op[3]);
  not not_67 (not_67_out, op[2]);
  not not_68 (not_68_out, op[0]);
  not not_69 (not_69_out, op[3]);
  not not_70 (not_70_out, op[2]);
  not not_71 (not_71_out, op[3]);
  not not_72 (not_72_out, op[3]);
  not not_73 (not_73_out, op[2]);
  not not_74 (not_74_out, op[2]);
  not not_75 (not_75_out, op[5]);
  not not_76 (not_76_out, op[3]);
  not not_77 (not_77_out, op[1]);
  not not_78 (not_78_out, op[2]);
  and and_1 (and_1_out, not_1_out, not_2_out, not_3_out, not_4_out);
  and and_2 (and_2_out, not_5_out, not_6_out, not_7_out);
  and and_3 (and_3_out, not_8_out, not_9_out, not_10_out);
  and and_4 (and_4_out, not_11_out, not_12_out, not_13_out);
  and and_5 (and_5_out, op[4], not_14_out, not_15_out);
  and and_6 (and_6_out, not_16_out, not_17_out, not_18_out);
  and and_7 (and_7_out, not_19_out, not_20_out, op[3]);
  and and_8 (and_8_out, not_21_out, op[3], not_22_out);
  and and_9 (and_9_out, not_23_out, op[3], not_24_out);
  and and_10 (and_10_out, not_25_out, op[3], op[2]);
  and and_11 (and_11_out, op[4], not_26_out);
  and and_12 (and_12_out, op[4], not_27_out, not_28_out);
  and and_13 (and_13_out, op[5], not_29_out, not_30_out);
  and and_14 (and_14_out, op[5], not_31_out, not_32_out, op[1], op[0]);
  and and_15 (and_15_out, not_33_out, not_34_out);
  and and_16 (and_16_out, op[1], not_35_out);
  and and_17 (and_17_out, not_36_out, not_37_out, not_38_out, op[2], not_39_out);
  and and_18 (and_18_out, op[4], not_40_out);
  and and_19 (and_19_out, op[5], not_41_out);
  and and_20 (and_20_out, op[5], not_42_out, not_43_out, op[1]);
  and and_21 (and_21_out, not_44_out, not_45_out, not_46_out, op[0]);
  and and_22 (and_22_out, not_47_out, not_48_out, not_49_out, op[0]);
  and and_23 (and_23_out, not_50_out, not_51_out, not_52_out, op[2], not_53_out, not_54_out);
  and and_24 (and_24_out, op[4], not_55_out, not_56_out, op[0]);
  and and_25 (and_25_out, not_57_out, op[2], not_58_out, op[0]);
  and and_26 (and_26_out, op[4], not_59_out, op[2], not_60_out);
  or or_2 (bne, and_25_out, and_26_out, and_27_out);
  and and_27 (and_27_out, op[5], not_61_out, op[2], not_62_out);
  and and_28 (and_28_out, not_63_out, not_64_out, not_65_out, op[1]);
  or or_3 (j, and_28_out, and_29_out, and_30_out);
  and and_29 (and_29_out, not_66_out, not_67_out, not_68_out, op[1]);
  and and_30 (and_30_out, op[4], not_69_out, not_70_out, op[1]);
  and and_31 (and_31_out, op[4], not_71_out);
  or or_4 (memR, and_31_out, and_32_out);
  and and_32 (and_32_out, op[5], not_72_out, not_73_out, op[0], op[1]);
  and and_33 (and_33_out, op[4], op[3]);
  or or_5 (memW, and_33_out, and_34_out);
  and and_34 (and_34_out, op[5], op[3], not_74_out, op[0], op[1]);
  and and_35 (and_35_out, not_75_out, not_76_out, op[2], not_77_out);
  or or_6 (memReg, and_35_out, op[4], and_36_out);
  and and_36 (and_36_out, op[5], not_78_out, op[1], op[0]);
  or or_7 (rd, and_1_out, and_2_out, and_3_out, and_4_out, and_5_out);
  or or_8 (wen, and_6_out, and_7_out, and_8_out, and_9_out, and_10_out, and_11_out, and_12_out, and_13_out, and_14_out);
  or or_9 (ext, and_15_out, and_16_out, and_17_out, and_18_out, and_19_out, and_20_out);
  or or_10 (beq, and_21_out, and_22_out, and_23_out, and_24_out);
endmodule

module zero (
  input  [31:0] D,
  output Z
);

  nor nor_1 (Z, D[0], D[1], D[2], D[3], D[4], D[5], D[6], D[7], D[8], D[9], D[10], D[11], D[12], D[13], D[14], D[15], D[16], D[17], D[18], D[19], D[20], D[21], D[22], D[23], D[24], D[25], D[26], D[27], D[28], D[29], D[30], D[31]);
endmodule

module aluFunct (
  input  f0,
  input  f1,
  input  f2,
  input  f3,
  input  f4,
  input  f5,
  output o0,
  output o1,
  output o2,
  output o3
);

  wire not_1_out;

  and and_1 (o2, f0, f5);
  not not_1 (not_1_out, f0);
  and and_2 (o3, not_1_out, f5);

  assign o0 = f3;
  assign o1 = f4;
endmodule

module aluOp (
  input  op0,
  input  op1,
  input  op2,
  input  op3,
  input  op4,
  input  op5,
  output o0,
  output o1,
  output o2,
  output o3
);

  wire and_2_out, and_3_out, not_1_out, not_2_out, not_3_out, not_4_out;

  and and_1 (o0, op2, op3);
  not not_1 (not_1_out, op2);
  not not_2 (not_2_out, op4);
  not not_3 (not_3_out, op5);
  not not_4 (not_4_out, op2);
  and and_2 (and_2_out, not_1_out, not_2_out);
  and and_3 (and_3_out, op4, not_3_out);
  or or_1 (o2, not_4_out, op5);
  or or_2 (o1, and_2_out, and_3_out);

  assign o3 = 1'b0;
endmodule

module aluctrl (
  input  [5:0] opcode,
  input  [5:0] funct,
  output [3:0] ctrl
);

  wire nor_1_out;
  wire [3:0] alufunct_1_o3, aluop_1_o3;

  nor nor_1 (nor_1_out, opcode[5], opcode[4], opcode[3], opcode[2], opcode[1], opcode[0]);
  aluOp aluop_1 (
    .op0(opcode[5]), .op1(opcode[4]), .op2(opcode[3]), .op3(opcode[2]), .op4(opcode[1]), .op5(opcode[0]),
    .o0(aluop_1_o3[3]), .o1(aluop_1_o3[2]), .o2(aluop_1_o3[1]), .o3(aluop_1_o3[0]));
  aluFunct alufunct_1 (
    .f0(funct[5]), .f1(funct[4]), .f2(funct[3]), .f3(funct[2]), .f4(funct[1]), .f5(funct[0]),
    .o0(alufunct_1_o3[3]), .o1(alufunct_1_o3[2]), .o2(alufunct_1_o3[1]), .o3(alufunct_1_o3[0]));
  Multiplexer #(.width(4), .enable("false")) multiplexer_1 (
    .in0(aluop_1_o3), .in1(alufunct_1_o3), .out(ctrl), .sel(nor_1_out));
endmodule

module nextPC (
  input  [31:0] PC,
  input  beq,
  input  bne,
  input  [25:0] imm,
  input  j,
  input  [31:0] zer0,
  output [31:0] nextPC
);

  wire and_1_out, and_2_out, or_1_out, zero_1_z;
  wire [3:0] incrementer_1_p2;
  wire [25:0] incrementer_1_p2_2;
  wire [29:0] adder_1_out, bit_extender_1_out, multiplexer_1_out;

  // Incrementer #(.width(30)) incrementer_1: pin names not known; wires that end beside it: PC[31:2], {incrementer_1_p2, incrementer_1_p2_2}
  assign bit_extender_1_out = {{14{imm[15]}}, imm[15:0]};  // Bit_Extender bit_extender_1
  Adder #(.width(30)) adder_1 (
    .a({incrementer_1_p2, incrementer_1_p2_2}), .b(bit_extender_1_out), .out(adder_1_out));  // open: cin, cout
  Multiplexer #(.width(30), .enable("false")) multiplexer_1 (
    .in0(adder_1_out), .in1({incrementer_1_p2, imm}), .out(multiplexer_1_out), .sel(j));
  Multiplexer #(.width(30), .enable("false")) multiplexer_2 (
    .in0({incrementer_1_p2, incrementer_1_p2_2}), .in1(multiplexer_1_out), .out(nextPC[31:2]), .sel(or_1_out));
  and and_1 (and_1_out, ~zero_1_z, bne);  // AND_Gate
  zero zero_1 (.Z(zero_1_z), .D(zer0));
  or or_1 (or_1_out, and_1_out, j, and_2_out);
  and and_2 (and_2_out, zero_1_z, beq);

  assign nextPC[1:0] = 2'b00;
endmodule
